# Fritzing sketch power_board (saved by Fritzing 0.8.5b)
circuit board: 10.296cm x 8.23954cm
breadboards: 1

parts:
  CONN1 = USB connector [package=THT]  # not connected
  OUTPUT = screw terminal, 4 pins
  INPUT = screw terminal, 4 pins
  Q1 = NPN-Transistor [package="TO92 [THT]"]
  R1 = Resistor [tolerance=±5% resistance=220 package=THT]
  RPI_GPIO = double row male pin header, 26 pins [form="♂ (male)"]

nets:
  N1: OUTPUT.pin1, INPUT.pin1
  N2: OUTPUT.pin2, INPUT.pin2, R1.Pin_0
  GND: OUTPUT.pin4, INPUT.pin4, Q1.E, RPI_GPIO.pin6
  N3: Q1.B, R1.Pin_1
  N4: Q1.C, RPI_GPIO.pin18
